// Logisim project M32.circ as structural Verilog
module PC (
  input  [31:0] INPT,
  input  WR,
  output [31:0] OUTPT
);

  wire CLK_out;
  wire [31:0] register_1_q;

  Clock CLK (.out(CLK_out));
  Register #(.width(32)) register_1 (.D(INPT), .en(WR), .clk(CLK_out), .Q(register_1_q));  // open: clr
  Multiplexer #(.width(32)) multiplexer_1 (.in0({32{1'b0}}), .in1(register_1_q), .out(OUTPT));  // open: sel

  // Notes on the sheet:
  //   Programar gnd_vcc
endmodule
